# Fritzing sketch SmartWatt (saved by Fritzing 0.9.5d)

parts:
  esp1 = ESP32 DevKitc V4
  Part1 = ACS712 Current Sensor 5A 20A 30A
  RY1 = SSR-40VA
  esp2 = ESP32 DevKitc V4
  Part2 = ACS712 Current Sensor 5A 20A 30A

nets:
  N1: esp1.IO5, RY1.Pin_3
  GND: esp1.GND, Part1.GND, RY1.Pin_4
  N2: esp1.IO12, Part1.2, Part1.OUT
  5V: esp1.5V, Part1.VCC
  GND_2: esp2.GND, Part2.GND
  N3: esp2.IO12, Part2.2, Part2.OUT
  5V_2: esp2.5V, Part2.VCC

custom parts:
  ESP32 DevKitc V4: ESP32-DevKitC board with ESP32-WROOM-32 module. ESP32-DevKitC V4 is a small-sized ESP32-based development board produced by Espressif. Most of the pins on the ESP module are broken out to the pin headers on the board. The pins D0, D1, D2, D3, CMD and CLK are used internally for communication between ESP32 and SPI flash memory. They are grouped on both sides near the USB connector. Avoid using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
  ACS712 Current Sensor 5A 20A 30A: Remix by Michael Kubina http://www.kubina.info Original by: https://forum.fritzing.org/t/current-sensor-5a-acs712/7694 https://forum.fritzing.org/u/ArtHome ArtHome12@gmail.com
  SSR-40VA: SSR-40VA solid state relay.
